# Fritzing sketch OpiaPlan (saved by Fritzing 0.9.2b)
breadboards: 1

parts:
  U1 = mystery part, 3 pins [chip_label="Hall Effect Sensor"]
  R3 = Resistor [tolerance=±5% resistance=10k package=THT]
  R2 = Trimmer Potentiometer [maximum_resistance=10kΩ package=THT]
  Leonardo = Arduino Leonardo (Rev3b)
  R1 = Trimmer Potentiometer [maximum_resistance=10kΩ package=THT]

nets:
  3.3V: U1.pin1, R3.Pin_0, Leonardo.3V3
  GND: U1.pin2, R2.leg2, Leonardo.GND, R1.leg2
  N1: U1.pin3, R3.Pin_1, Leonardo.D2/SDA
  5V: R2.leg1, Leonardo.5V, R1.leg1
  N2: R2.wiper, Leonardo.A3
  N3: Leonardo.A2, R1.wiper
